// Logisim project 0606_2.circ as structural Verilog: 2 circuits, main circuit main
module main (
  input  in_1,
  input  in_2,
  input  [1:0] in_3,
  input  a,
  input  b,
  output carryin,
  output out_7,
  output out_8
);

  wire adder_1_out, and_1_out, multiplexer_1_out, multiplexer_2_out, not_1_out, not_2_out, or_1_out;

  not not_1 (not_1_out, a);
  not not_2 (not_2_out, b);
  Multiplexer #(.enable("false")) multiplexer_1 (.in0(a), .in1(not_1_out), .out(multiplexer_1_out), .sel(in_1));
  Multiplexer #(.enable("false")) multiplexer_2 (.in0(b), .in1(not_2_out), .out(multiplexer_2_out), .sel(in_2));
  and and_1 (and_1_out, multiplexer_1_out, multiplexer_2_out);
  or or_1 (or_1_out, multiplexer_1_out, multiplexer_2_out);
  Adder #(.width(1)) adder_1 (
    .a(multiplexer_1_out), .b(multiplexer_2_out), .out(adder_1_out), .cin(carryin), .cout(out_8));
  Multiplexer #(.select(2), .enable("false")) multiplexer_3 (
    .in0(and_1_out), .in1(or_1_out), .in2(adder_1_out), .out(out_7), .sel(in_3));  // open: in3

  // Notes on the sheet:
  //   Ainvert
  //   Binvert
  //   operation
endmodule

module _4_bit_ALU (
  input  in_1,
  input  in_2,
  input  in_3,
  input  [1:0] in_4,
  input  in_5,
  input  in_6,
  input  in_7,
  input  in_8,
  input  in_9,
  input  in_10,
  input  in_11,
  input  in_12,
  output out_13,
  output out_14,
  output out_15,
  output out_16
);

  wire main_1_p5, main_2_p5, main_3_p5, main_4_p5;

  // main main_1: pin names not known; wires that end beside it: in_5, in_6, in_2, in_3, main_1_p5, in_4, out_13
  // main main_2: pin names not known; wires that end beside it: in_7, in_8, in_2, main_1_p5, main_2_p5, in_4, out_14
  // main main_3: pin names not known; wires that end beside it: in_9, in_10, in_2, main_2_p5, main_3_p5, in_4, out_15
  // main main_4: pin names not known; wires that end beside it: in_11, in_12, in_2, main_3_p5, main_4_p5, in_4
endmodule
