// Logisim project 4-bit-cpu.circ as structural Verilog: 1 circuit, main circuit main
module main (
  input  [3:0] in_1,
  input  in_2,
  input  in_3,
  input  in_4
);

  wire clock_1_out, demultiplexer_1_out0, demultiplexer_1_out1, demultiplexer_1_out2, demultiplexer_1_out3;
  wire [0:0] rom_1_data_2;
  wire [1:0] multiplexer_2_out;
  wire [3:0] adder_1_out, multiplexer_3_out, multiplexer_4_out, multiplexer_5_out, multiplexer_6_out,
       n4_bit_alu_1_p7, ram_1_data, register_1_q, register_2_q, register_3_q, register_4_q, register_5_q;
  wire [3:1] rom_1_data_3;
  wire [4:0] rom_3_data;
  wire [9:5] rom_1_data;

  Clock clock_1 (.out(clock_1_out));
  Multiplexer #(.enable("false")) multiplexer_1 (
    .in0(adder_1_out[0]), .in1(rom_1_data_2[0]), .sel(rom_1_data_3[3]));  // open: out
  Register #(.width(4)) register_1 (.en(in_2), .Q(register_1_q), .clk(clock_1_out));  // open: D, clr
  Adder #(.width(4)) adder_1 (.a(in_1), .b(register_1_q), .out(adder_1_out));  // open: cin, cout
  ROM #(.addrWidth(4), .dataWidth(10)) rom_1 (
    .addr(register_1_q), .data({rom_1_data, rom_1_data[5], rom_1_data_2[0], {3{rom_1_data_3[1]}}}),
    .sel(rom_1_data[7]));
  ROM #(.addrWidth(2), .dataWidth(9)) rom_2 (
    .addr({rom_1_data[8], rom_1_data[9]}), .data({9{rom_1_data_3[3]}}), .sel(rom_1_data[7]));
  Multiplexer #(.width(2), .enable("false")) multiplexer_2 (
    .in0({2{rom_1_data[5]}}), .in1({rom_1_data_2[0], rom_1_data_3[1]}), .out(multiplexer_2_out),
    .sel(rom_1_data_3[3]));
  Demultiplexer #(.select(2)) demultiplexer_1 (
    .out0(demultiplexer_1_out0), .out1(demultiplexer_1_out1), .out2(demultiplexer_1_out2),
    .out3(demultiplexer_1_out3), .in(rom_1_data_3[3]), .en(multiplexer_2_out[0]));  // open: sel
  Multiplexer #(.enable("false")) multiplexer_3 (
    .in0(n4_bit_alu_1_p7[0]), .in1(ram_1_data[0]), .out(multiplexer_3_out[0]), .sel(rom_1_data_3[3]));
  Register #(.width(4)) register_2 (
    .D(multiplexer_3_out), .en(demultiplexer_1_out0), .Q(register_2_q), .clk(clock_1_out));  // open: clr
  Register #(.width(4)) register_3 (
    .D(multiplexer_3_out), .Q(register_3_q), .clk(demultiplexer_1_out1));  // open: en, clr
  Register #(.width(4)) register_4 (
    .D(multiplexer_3_out), .en(demultiplexer_1_out2), .Q(register_4_q), .clk(clock_1_out));  // open: clr
  Register #(.width(4)) register_5 (
    .D(multiplexer_3_out), .en(demultiplexer_1_out3), .Q(register_5_q), .clk(clock_1_out));  // open: clr
  ROM #(.addrWidth(4), .dataWidth(5)) rom_3 (
    .addr({{2{rom_1_data_3[3]}}, {2{rom_1_data_3[1]}}}), .data(rom_3_data), .sel(in_4));
  Multiplexer #(.select(2), .width(4), .enable("false")) multiplexer_4 (
    .in0(register_2_q), .in1(register_3_q), .in2(register_4_q), .in3(register_5_q), .out(multiplexer_4_out),
    .sel({rom_1_data[6], rom_1_data[7]}));
  Multiplexer #(.select(2), .width(4), .enable("false")) multiplexer_5 (
    .in0(register_2_q), .in1(register_3_q), .in2(register_4_q), .in3(register_5_q), .out(multiplexer_5_out),
    .sel({2{rom_1_data[5]}}));
  Multiplexer #(.width(4), .enable("false")) multiplexer_6 (
    .in0(multiplexer_5_out), .in1({{3{rom_1_data_3[1]}}, rom_1_data_2[0]}), .out(multiplexer_6_out),
    .sel(rom_1_data_3[3]));
  // _4_bit_alu 4_bit_alu_1: pin names not known; wires that end beside it: multiplexer_4_out, multiplexer_6_out, rom_3_data[0], rom_3_data[1], rom_3_data[2], rom_3_data[4:3], n4_bit_alu_1_p7
  RAM #(.addrWidth(4), .dataWidth(4), .bus("separate")) ram_1 (
    .addr(n4_bit_alu_1_p7), .din(multiplexer_5_out), .data(ram_1_data), .str(rom_1_data_3[3]), .sel(in_4),
    .clk(clock_1_out), .ld(rom_1_data_3[3]));  // open: clr
  // Pins of 1 and 4 bits meet at {{3{rom_1_data_3[1]}}, rom_1_data_2[0]}
  // Pins of 1 and 4 bits meet at n4_bit_alu_1_p7
  // Pins of 1 and 4 bits meet at ram_1_data
  // Pins of 1 and 4 bits meet at multiplexer_3_out
  // Pins of 1 and 2 bits meet at multiplexer_2_out
  // Pins of 1 and 4 bits meet at adder_1_out

  // Notes on the sheet:
  //   contents of rom_1 (hex, n*v repeats v):
  //   110 121 6e 231 300
  //   contents of rom_2 (hex, n*v repeats v):
  //   122 f0 88 4
  //   contents of rom_3 (hex, n*v repeats v):
  //   4*10 5*0 8 10 16
endmodule
